# Fritzing sketch schematic (saved by Fritzing 0.9.3b)
perfboards: 2

parts:
  Part1 = Arduino Mega ADK (Rev3)
  Part2 = Monster Moto Shield
  Part3 = Monster Moto Shield
  HC-SR04_Sensor_1 = HC-SR04 Ultrasonic Distance Sensor
  HC-SR04_Sensor_2 = HC-SR04 Ultrasonic Distance Sensor
  HC-SR04_Sensor_3 = HC-SR04 Ultrasonic Distance Sensor
  HC-SR04_Sensor_4 = HC-SR04 Ultrasonic Distance Sensor
  HC-SR04_Sensor_5 = HC-SR04 Ultrasonic Distance Sensor
  J1 = Basic Servo
  M1 = DC Motor
  M2 = DC Motor
  M3 = DC Motor
  e-radionica1 = TCS230 Color Sensor [part_number=101209]
  e-radionica2 = TCS230 Color Sensor [part_number=101209]
  R4 = Photocell (LDR) [package=THT]
  R6 = Resistor [tolerance=±5% resistance=220 package="0603 [SMD]"]
  R7 = Photocell (LDR) [package=THT]
  R8 = Resistor [tolerance=±5% resistance=220 package="0603 [SMD]"]
  R9 = Photocell (LDR) [package=THT]
  R10 = Resistor [tolerance=±5% resistance=220 package="0603 [SMD]"]
  R11 = Photocell (LDR) [package=THT]
  R12 = Resistor [tolerance=±5% resistance=220 package="0603 [SMD]"]
  R13 = Photocell (LDR) [package=THT]
  R14 = Resistor [tolerance=±5% resistance=220 package="0603 [SMD]"]
  LED1 = LED - 5mm [color="Red (633nm)" package="5 mm [THT]"]
  R15 = Resistor [tolerance=±5% resistance=220 package="0603 [SMD]"]
  R16 = Resistor [tolerance=±5% resistance=220 package="0603 [SMD]"]
  LED2 = LED - 5mm [color="Red (633nm)" package="5 mm [THT]"]
  LED3 = LED - 5mm [color="Red (633nm)" package="5 mm [THT]"]
  LED4 = LED - 5mm [color="Red (633nm)" package="5 mm [THT]"]
  LED5 = LED - 5mm [color="Red (633nm)" package="5 mm [THT]"]
  R17 = Resistor [tolerance=±5% resistance=220 package="0603 [SMD]"]
  R18 = Resistor [tolerance=±5% resistance=220 package="0603 [SMD]"]
  R19 = Resistor [tolerance=±5% resistance=220 package="0603 [SMD]"]
  R20 = Photocell (LDR) [package=THT]
  R21 = Photocell (LDR) [package=THT]
  R22 = Photocell (LDR) [package=THT]
  R23 = Photocell (LDR) [package=THT]
  R24 = Photocell (LDR) [package=THT]
  R25 = Resistor [tolerance=±5% resistance=220 package="0603 [SMD]"]
  R26 = Resistor [tolerance=±5% resistance=220 package="0603 [SMD]"]
  R27 = Resistor [tolerance=±5% resistance=220 package="0603 [SMD]"]
  R28 = Resistor [tolerance=±5% resistance=220 package="0603 [SMD]"]
  R29 = Resistor [tolerance=±5% resistance=220 package="0603 [SMD]"]
  R30 = Resistor [tolerance=±5% resistance=220 package="0603 [SMD]"]
  R31 = Resistor [tolerance=±5% resistance=220 package="0603 [SMD]"]
  R32 = Resistor [tolerance=±5% resistance=220 package="0603 [SMD]"]
  R33 = Resistor [tolerance=±5% resistance=220 package="0603 [SMD]"]
  R34 = Resistor [tolerance=±5% resistance=220 package="0603 [SMD]"]
  LED6 = LED - 5mm [color="Red (633nm)" package="5 mm [THT]"]
  LED7 = LED - 5mm [color="Red (633nm)" package="5 mm [THT]"]
  LED8 = LED - 5mm [color="Red (633nm)" package="5 mm [THT]"]
  LED9 = LED - 5mm [color="Red (633nm)" package="5 mm [THT]"]
  LED10 = LED - 5mm [color="Red (633nm)" package="5 mm [THT]"]
  J2 = Dagu DGServo 9g header (male) [package=THT]
  J3 = Dagu DGServo 9g header (male) [package=THT]
  J4 = Piezo Speaker
  S1 = Toggle Switch [package=THT]
  S2 = Toggle Switch [package=THT]
  S3 = Toggle Switch [package=THT]
  S4 = Toggle Switch [package=THT]
  Part4 = LED Tactile Button Breakout v10 [part_number=BOB-10467]
  LED11 = LED - 3mm [color="Red (633nm)" package="3 mm [THT]"]
  LED12 = LED - 3mm [color="Red (633nm)" package="3 mm [THT]"]

nets:
  N1: Part1.A8, R24.pin_1, R25.Pin_1
  N2: Part1.A9, R20.pin_1, R34.Pin_1
  N3: Part1.A10, R22.pin_1, R30.Pin_1
  N4: Part1.A11, R23.pin_1, R27.Pin_1
  N5: Part1.A12, R21.pin_1, R28.Pin_1
  N6: Part1.A0, Part2.EN1_-_A0
  N7: Part1.A1, Part2.EN2_-_A1
  N8: Part1.A2, Part3.EN1_-_A0
  N9: Part1.A3, R4.pin_1, R6.Pin_1
  N10: Part1.A4, R7.pin_1, R8.Pin_1
  N11: Part1.A5, R9.pin_1, R10.Pin_1
  N12: Part1.A6, R11.pin_1, R12.Pin_1
  N13: Part1.A7, R13.pin_1, R14.Pin_1
  N14: Part1.D19/RX1, Part2.INB1_-_D8
  N15: Part1.D18/TX1, Part2.INA1_-_D7
  N16: Part1.D12_PWM, J1.pulse
  N17: Part1.D10_PWM, Part4.4
  N18: Part1.D9_PWM, LED11.anode
  N19: Part1.D8_PWM, LED12.anode
  N20: Part1.D2_PWM, J3.gnd
  N21: Part1.D3_PWM, J2.gnd
  N22: Part1.D4_PWM, J4.pin2
  N23: Part1.D5_PWM, Part2.PWM1_-_D5
  N24: Part1.D6_PWM, Part2.PWM2_-_D6
  N25: Part1.D7_PWM, Part3.PWM1_-_D5
  N26: Part1.D22, S1.L1
  N27: Part1.D23, S2.L1
  N28: Part1.D24, S3.L1
  N29: Part1.D25, S4.L1
  N30: Part1.D26, e-radionica2.S0
  N31: Part1.D27, e-radionica2.S1
  N32: Part1.D28, e-radionica2.S2
  N33: Part1.D29, e-radionica2.S3
  N34: Part1.D32, e-radionica1.S0
  N35: Part1.D33, e-radionica1.S1
  N36: Part1.D34, e-radionica1.S2
  N37: Part1.D35, e-radionica1.S3
  N38: Part1.D36, e-radionica1.Out
  N39: Part1.D40, Part2.INA2_-_D4
  N40: Part1.D41, Part2.INB2_-_D9
  N41: Part1.D42, Part3.INA1_-_D7
  N42: Part1.D43, Part3.INB1_-_D8
  N43: Part1.D44, HC-SR04_Sensor_5.TRIG
  N44: Part1.D45, HC-SR04_Sensor_5.ECHO
  N45: Part1.D46, HC-SR04_Sensor_2.TRIG
  N46: Part1.D47, HC-SR04_Sensor_2.ECHO
  N47: Part1.D48, HC-SR04_Sensor_4.TRIG
  N48: Part1.D49, HC-SR04_Sensor_4.ECHO
  N49: Part1.D50/MISO, HC-SR04_Sensor_3.TRIG
  N50: Part1.D51/MOSI, HC-SR04_Sensor_3.ECHO
  N51: Part1.D52/SCK, HC-SR04_Sensor_1.TRIG
  N52: Part1.D53/SS, HC-SR04_Sensor_1.ECHO
  N53: Part2.OUTA1, M1.pin_1
  N54: Part2.OUTA2, M2.pin_1
  N55: Part2.OUTB2, M2.pin_2
  N56: Part3.OUTA1, M3.pin_1
  N57: Part3.OUTB1, M3.pin_2
  N58: R4.pin_0, R7.pin_0, R9.pin_0, R11.pin_0, R13.pin_0, R15.Pin_1, R16.Pin_1, R17.Pin_1, R18.Pin_1, R19.Pin_1
  N59: R6.Pin_0, R8.Pin_0, R10.Pin_0, R12.Pin_0, R14.Pin_0, LED1.anode, LED2.anode, LED3.anode, LED4.anode, LED5.anode
  N60: LED1.cathode, R15.Pin_0
  N61: R16.Pin_0, LED2.cathode
  N62: LED3.cathode, R17.Pin_0
  N63: LED4.cathode, R18.Pin_0
  N64: LED5.cathode, R19.Pin_0
  N65: R20.pin_0, R21.pin_0, R22.pin_0, R23.pin_0, R24.pin_0, R26.Pin_1, R29.Pin_1, R31.Pin_1, R32.Pin_1, R33.Pin_1
  N66: R25.Pin_0, R27.Pin_0, R28.Pin_0, R30.Pin_0, R34.Pin_0, LED6.anode, LED7.anode, LED8.anode, LED9.anode, LED10.anode
  N67: R26.Pin_0, LED10.cathode
  N68: R29.Pin_0, LED8.cathode
  N69: R31.Pin_0, LED9.cathode
  N70: R32.Pin_0, LED7.cathode
  N71: R33.Pin_0, LED6.cathode

notes:
  Motor Encoder Output
  Locomotion Motor 1
  Locomotion Motor 2
  Arm Motor
  Arrow Follow Sensor Panel 1
  Arrow Follow Sensor Panel 2
  Note: None of the components are connected to power nor ground in order to avoid schematic complexity. You may connect those to appropriate connectors in your build

custom parts:
  TCS230 Color Sensor: TCS230
